# Fritzing sketch Mega-Photoresistor (saved by Fritzing 0.9.3b)
breadboards: 1

parts:
  Arduino_Mega = Arduino Mega 2560 (Rev3)
  Photoresistor = PHOTOCELL [package=photocell]
  R1 = Resistor [tolerance=±5% resistance=220 package=THT]

nets:
  N1: Arduino_Mega.A0, Photoresistor.P$2, R1.Pin_1
  N2: Arduino_Mega.GND, R1.Pin_0
  N3: Arduino_Mega.5V, Photoresistor.P$1
