# Fritzing sketch System (saved by Fritzing 0.9.3b)
breadboards: 1

parts:
  8V_Regulated_Output = Voltage Regulator - Variable [package="TO220 [THT]"]
  5V_Regulated_Output = Voltage Regulator - Variable [package="TO220 [THT]"]
  3_3V_Regulated_Output = Voltage Regulator - Variable [package="TO220 [THT]"]
  Arduino_Mega = Arduino Mega 2560 (Rev3)
  Relay = RELAY [package=relay-jzc]
  Laser_Diode = Luxeon LED [package=luxeon]
  5V_USB_input = Raspberry Pi 3 [part_number=RPI-3-V1.2]
  Photoresistor = PHOTOCELL [package=photocell-kit]
  LED_Display = LCD-16X2 [package=lcd-16x2_nosilk]
  Start_Button = Round Pushbutton
  Finish_Button = Round Pushbutton
  Pulldown_Resistor = Resistor [tolerance=±5% resistance=220 package="2512 [SMD]"]

nets:
  N1: 8V_Regulated_Output.OUT, 5V_Regulated_Output.IN, Arduino_Mega.VIN
  12V: 8V_Regulated_Output.IN
  N2: 5V_Regulated_Output.OUT, 3_3V_Regulated_Output.IN, Photoresistor.P$1, Start_Button.leg1
  N3: 3_3V_Regulated_Output.OUT, Relay.NC
  N4: Arduino_Mega.A0, Photoresistor.P$2, Pulldown_Resistor.Pin_1
  N5: Arduino_Mega.D19/RX1, 5V_USB_input.GIPO14
  N6: Arduino_Mega.D18/TX1, 5V_USB_input.GIPO15
  N7: Arduino_Mega.D12_PWM, Relay.COIL1
  N8: Arduino_Mega.D10_PWM, Start_Button.leg0
  GND: Arduino_Mega.GND, Relay.COIL2, Laser_Diode.C, 5V_USB_input.GND, Pulldown_Resistor.Pin_0
  N9: Arduino_Mega.D7_PWM, Finish_Button.leg0
  N10: Relay.NO, Laser_Diode.A
  N11: 5V_USB_input.GPIO2, LED_Display.A
  N12: 5V_USB_input.GPIO3, LED_Display.DB7
  N13: 5V_USB_input.GIPO4, LED_Display.DB6
  N14: 5V_USB_input.GIPO17, LED_Display.DB5
  N15: 5V_USB_input.GIPO27, LED_Display.DB4
  N16: 5V_USB_input.GIPO22, LED_Display.DB3
  N17: 5V_USB_input.GIPO10, LED_Display.DB2
  N18: 5V_USB_input.GIPO9, LED_Display.DB1
  N19: 5V_USB_input.GIPO11, LED_Display.DB0
  N20: 5V_USB_input.ID_SD, LED_Display.E
  N21: 5V_USB_input.GIPO5, LED_Display.R_W
  N22: 5V_USB_input.GIPO6, LED_Display.RS
  N23: 5V_USB_input.GIPO13, LED_Display.VO
  N24: 5V_USB_input.GIPO19, LED_Display.VDD
  N25: 5V_USB_input.GIPO26, LED_Display.VSS
  N26: 5V_USB_input.GIPO21, LED_Display.K
  N27: 5V_USB_input.5V, Finish_Button.leg1
