# Fritzing sketch mi-system-circuit (saved by Fritzing 0.9.3b)
breadboards: 1

parts:
  Arduino_Mega = Arduino Mega 2560 (Rev3)
  Photoresistor = PHOTOCELL [package=photocell]
  R1 = Resistor [tolerance=±5% resistance=220 package=THT]
  Photoresistor1 = PHOTOCELL [package=photocell]
  Photoresistor2 = PHOTOCELL [package=photocell]
  Photoresistor3 = PHOTOCELL [package=photocell]
  Photoresistor4 = PHOTOCELL [package=photocell]
  Photoresistor5 = PHOTOCELL [package=photocell]
  Photoresistor6 = PHOTOCELL [package=photocell]
  Photoresistor7 = PHOTOCELL [package=photocell]
  Photoresistor8 = PHOTOCELL [package=photocell]
  Photoresistor9 = PHOTOCELL [package=photocell]
  R2 = Resistor [tolerance=±5% resistance=220 package=THT]
  R3 = Resistor [tolerance=±5% resistance=220 package=THT]
  R4 = Resistor [tolerance=±5% resistance=220 package=THT]
  R5 = Resistor [tolerance=±5% resistance=220 package=THT]
  R6 = Resistor [tolerance=±5% resistance=220 package=THT]
  R7 = Resistor [tolerance=±5% resistance=220 package=THT]
  R8 = Resistor [tolerance=±5% resistance=220 package=THT]
  R9 = Resistor [tolerance=±5% resistance=220 package=THT]
  R10 = Resistor [tolerance=±5% resistance=220 package=THT]

nets:
  N1: Arduino_Mega.A8, Photoresistor8.P$2, R9.Pin_1
  N2: Arduino_Mega.A9, Photoresistor9.P$2, R10.Pin_1
  N3: Arduino_Mega.A0, Photoresistor.P$2, R1.Pin_1
  N4: Arduino_Mega.A1, Photoresistor1.P$2, R2.Pin_1
  N5: Arduino_Mega.A2, Photoresistor2.P$2, R3.Pin_1
  N6: Arduino_Mega.A3, Photoresistor3.P$2, R4.Pin_1
  N7: Arduino_Mega.A4, Photoresistor4.P$2, R5.Pin_1
  N8: Arduino_Mega.A5, Photoresistor5.P$2, R6.Pin_1
  N9: Arduino_Mega.A6, Photoresistor6.P$2, R7.Pin_1
  N10: Arduino_Mega.A7, Photoresistor7.P$2, R8.Pin_1
  N11: Arduino_Mega.5V, Photoresistor.P$1, Photoresistor1.P$1, Photoresistor2.P$1, Photoresistor3.P$1, Photoresistor4.P$1, Photoresistor5.P$1, Photoresistor6.P$1, Photoresistor7.P$1, Photoresistor8.P$1, Photoresistor9.P$1
  N12: Arduino_Mega.GND, R1.Pin_0, R2.Pin_0, R3.Pin_0, R5.Pin_0, R6.Pin_0, R7.Pin_0, R8.Pin_0, R9.Pin_0, R10.Pin_0
