# Fritzing sketch photoresistor-nest (saved by Fritzing 0.9.3b)
breadboards: 1

parts:
  Arduino_Mega = Arduino Mega 2560 (Rev3)
  R1 = Resistor [tolerance=±5% resistance=220 package=THT]
  R2 = Resistor [tolerance=±5% resistance=220 package=THT]
  R3 = Resistor [tolerance=±5% resistance=220 package=THT]
  R4 = Resistor [tolerance=±5% resistance=220 package=THT]
  R5 = Resistor [tolerance=±5% resistance=220 package=THT]
  R6 = Resistor [tolerance=±5% resistance=220 package=THT]
  R7 = Resistor [tolerance=±5% resistance=220 package=THT]
  R8 = Resistor [tolerance=±5% resistance=220 package=THT]
  R9 = Resistor [tolerance=±5% resistance=220 package=THT]
  R10 = Resistor [tolerance=±5% resistance=220 package=THT]
  PR1 = PHOTOCELL [package=photocell-kit]
  PR2 = PHOTOCELL [package=photocell-kit]
  PR3 = PHOTOCELL [package=photocell-kit]
  PR4 = PHOTOCELL [package=photocell-kit]
  PR5 = PHOTOCELL [package=photocell-kit]
  PR6 = PHOTOCELL [package=photocell-kit]
  PR7 = PHOTOCELL [package=photocell-kit]
  PR8 = PHOTOCELL [package=photocell-kit]
  PR9 = PHOTOCELL [package=photocell-kit]
  PR10 = PHOTOCELL [package=photocell-kit]
  Out_to_Relay = SWITCH-SPST-2 [package=switch-spst-vertical]
  In_from_Pi = Antenna
  Out_to_Pi = Antenna

nets:
  N1: Arduino_Mega.A8, R9.Pin_1, PR9.P$2
  N2: Arduino_Mega.A9, R10.Pin_1, PR10.P$2
  N3: Arduino_Mega.A0, R1.Pin_1, PR1.P$2
  N4: Arduino_Mega.A1, R2.Pin_1, PR2.P$2
  N5: Arduino_Mega.A2, R3.Pin_1, PR3.P$2
  N6: Arduino_Mega.A3, R4.Pin_1, PR4.P$2
  N7: Arduino_Mega.A4, R5.Pin_1, PR5.P$2
  N8: Arduino_Mega.A5, R6.Pin_1, PR6.P$2
  N9: Arduino_Mega.A6, R7.Pin_1, PR7.P$2
  N10: Arduino_Mega.A7, R8.Pin_1, PR8.P$2
  N11: Arduino_Mega.D19/RX1, In_from_Pi.antenna_lead
  N12: Arduino_Mega.D18/TX1, Out_to_Pi.antenna_lead
  N13: Arduino_Mega.GND, R1.Pin_0, R2.Pin_0, R3.Pin_0, R4.Pin_0, R5.Pin_0, R6.Pin_0, R7.Pin_0, R8.Pin_0, R9.Pin_0, R10.Pin_0
  N14: Arduino_Mega.5V, PR1.P$1, PR2.P$1, PR3.P$1, PR4.P$1, PR5.P$1, PR6.P$1, PR7.P$1, PR8.P$1, PR9.P$1, PR10.P$1
  N15: Arduino_Mega.D37, Out_to_Relay.O
